# Fritzing sketch HelloWorldBlink (saved by Fritzing 0.9.0b)
breadboards: 1

parts:
  R8 = Resistor [tolerance=±5% resistance=330 package=THT]
  LED1 = LED - 5mm [color="Blue (430nm)" package="5 mm [THT]"]
  PART1 = SparkFun Photon RedBoard [part_number=DEV-13321]

nets:
  N1: R8.Pin_0, LED1.cathode
  N2: R8.Pin_1, PART1.GND
  N3: LED1.anode, PART1.D0

custom parts:
  SparkFun Photon RedBoard: SparkFun RedBoard for Photon has the P1 module in an Arduino Uno R3 footprint. Please visit: www.sparkfun.com/products/13321
