# Fritzing sketch PlantMonitor (saved by Fritzing 0.8.7b)

parts:
  PART1 = SparkFun Photon RedBoard [part_number=DEV-13321]
  PART2 = SparkFun Soil Moisture Sensor [part_number=SEN-13322]

nets:
  N1: PART1.A5/SCL, PART1.A2, PART2.SIG
  GND: PART1.GND, PART2.GND
  N2: PART1.D6, PART2.VCC

custom parts:
  SparkFun Photon RedBoard: SparkFun RedBoard for Photon has the P1 module in an Arduino Uno R3 footprint. Please visit: www.sparkfun.com/products/13321
  SparkFun Soil Moisture Sensor: The SparkFun Soil Moisture Sensor is a simple breakout for measuring the moisture in soil and similar materials.
