# Fritzing sketch ColorSelector (saved by Fritzing 0.9.0b)
breadboards: 1

parts:
  PART1 = SparkFun RedBoard for Photon [part_number=DEV-13321]
  R1 = TRIMPOT [package=trimpot_pth_s3_lock]
  S4 = SWITCH-MOMENTARY-2 [package=tactile-pth-12mm]
  S5 = SWITCH-MOMENTARY-2 [package=tactile-pth-12mm]
  S6 = SWITCH-MOMENTARY-2 [package=tactile-pth-12mm]

nets:
  N1: PART1.A0, R1.WIPER
  N2: PART1.D4, S5.pin_3
  N3: PART1.D3, S4.pin_3
  N4: PART1.D2, S6.pin_3
  N5: R1.CW, S4.pin_4, S5.pin_4, S6.pin_4

custom parts:
  SparkFun RedBoard for Photon: SparkFun RedBoard for Photon has the P1 module in an Arduino Uno R3 footprint. Please visit: www.sparkfun.com/products/13321
  SWITCH-MOMENTARY-2: Various NO switches- pushbuttons, reed, etc
