# Fritzing sketch MusicTime (saved by Fritzing 0.9.0b)
breadboards: 1

parts:
  PART1 = SparkFun Photon RedBoard [part_number=DEV-13321]
  SG2 = Buzzer 12mm [package=buzzer-12mm-ns]

nets:
  N1: PART1.D2, SG2.1
  N2: PART1.GND, SG2.2

custom parts:
  SparkFun Photon RedBoard: SparkFun RedBoard for Photon has the P1 module in an Arduino Uno R3 footprint. Please visit: www.sparkfun.com/products/13321
  Buzzer 12mm: Buzzer 12mm Spark Fun Electronics SKU : Comp-Buzzer Through hole
