# Fritzing sketch environment-monitor-fritzing (saved by Fritzing 0.9.2b)
breadboards: 1

parts:
  PART1 = SparkFun Photon RedBoard [part_number=DEV-13321]
  RHT1 = Humidity and Temperature Sensor RHT03
  R1 = PHOTOCELL [package=photocell-kit]
  R2 = Resistor [tolerance=±5% resistance=330 package=THT]

nets:
  N1: PART1.A0, R1.P$1, R2.Pin_0
  N2: PART1.D3, RHT1.Data-signal
  3.3V: PART1.3.3V, RHT1.Vcc, R1.P$2
  N3: PART1.GND, RHT1.GND_2, R2.Pin_1

custom parts:
  SparkFun Photon RedBoard: SparkFun RedBoard for Photon has the P1 module in an Arduino Uno R3 footprint. Please visit: www.sparkfun.com/products/13321
