# Fritzing sketch AutomaticFishFeeder (saved by Fritzing 0.8.7b)
breadboards: 1

parts:
  PART1 = SparkFun Photon RedBoard [part_number=DEV-13321]
  J2 = Basic Servo
  S3 = SWITCH-MOMENTARY-2 [package=tactile-pth-12mm]

nets:
  N1: PART1.D1, S3.pin_3
  N2: PART1.D0, J2.pulse
  N3: PART1.V-USB, J2.vcc
  N4: PART1.GND#117, J2.gnd
  N5: PART1.GND#118, S3.pin_4

custom parts:
  SparkFun Photon RedBoard: SparkFun RedBoard for Photon has the P1 module in an Arduino Uno R3 footprint. Please visit: www.sparkfun.com/products/13321
  SWITCH-MOMENTARY-2: Various NO switches- pushbuttons, reed, etc
