# Fritzing sketch ActivityTracker (saved by Fritzing 0.9.2b)
breadboards: 1

parts:
  PART1 = SparkFun Photon RedBoard [part_number=DEV-13321]
  3-Axis_Accelerometer1 = 3-Axis Accelerometer Breakout - MMA8452Q
  S1 = SWITCH-MOMENTARY-2 [package=tactile-pth-12mm]

nets:
  N1: PART1.D1, 3-Axis_Accelerometer1.SCL
  N2: PART1.D0, 3-Axis_Accelerometer1.SDA
  N3: PART1.D3, S1.1
  3.3V: PART1.3.3V, 3-Axis_Accelerometer1.3.3V
  N4: PART1.GND#117, 3-Axis_Accelerometer1.GND
  N5: PART1.GND#118, S1.2

custom parts:
  SparkFun Photon RedBoard: SparkFun RedBoard for Photon has the P1 module in an Arduino Uno R3 footprint. Please visit: www.sparkfun.com/products/13321
  SWITCH-MOMENTARY-2: Various NO switches- pushbuttons, reed, etc
