# Fritzing sketch Pong (saved by Fritzing 0.9.0b)
breadboards: 1

parts:
  PART1 = SparkFun RedBoard for Photon [part_number=DEV-13321]
  R1 = Photocell (LDR) [package=THT]
  R3 = Resistor [tolerance=±5% resistance=330 package=THT]
  IC1 = OLED breakout [chip_label=IC package="DIP (Dual Inline) [THT]"]
  R4 = TRIMPOT [package=trimpot_pth_s3_lock]

nets:
  N1: PART1.A0, R1.pin_0, R3.Pin_1
  N2: PART1.A1, R4.WIPER
  N3: PART1.A2, IC1.pin1
  N4: PART1.A3, IC1.pin5
  N5: PART1.A5/SCL, IC1.pin6
  N6: PART1.D6, IC1.pin2
  N7: PART1.D5, IC1.pin3
  N8: R1.pin_1, IC1.pin7, R4.CCW
  N9: R3.Pin_0, IC1.pin8, R4.CW

custom parts:
  SparkFun RedBoard for Photon: SparkFun RedBoard for Photon has the P1 module in an Arduino Uno R3 footprint. Please visit: www.sparkfun.com/products/13321
  OLED breakout: A DIP stand-in part for whatever IC you want. With 16 pins on a 300mil dual inline package (DIP) footprint.
