# Fritzing sketch OLEDApps (saved by Fritzing 0.9.2b)
breadboards: 1

parts:
  PART1 = SparkFun Photon RedBoard [part_number=DEV-13321]
  IC1 = OLED breakout [chip_label=IC package="DIP (Dual Inline) [THT]"]
  S1 = SWITCH-MOMENTARY-2 [package=tactile-pth-12mm]
  S2 = SWITCH-MOMENTARY-2 [package=tactile-pth-12mm]
  S3 = SWITCH-MOMENTARY-2 [package=tactile-pth-12mm]

nets:
  N1: PART1.A4/SDA, PART1.A5, IC1.pin6
  N2: PART1.A3, IC1.pin5
  N3: PART1.A2, IC1.pin1
  N4: PART1.D6, IC1.pin2
  N5: PART1.D5, IC1.pin3
  N6: PART1.D4, S3.pin_3
  N7: PART1.D3, S2.pin_3
  N8: PART1.D2, S1.pin_3
  N9: PART1.3.3V, IC1.pin7
  N10: PART1.GND, IC1.pin8, S1.pin_4, S2.pin_4, S3.pin_4

custom parts:
  SparkFun Photon RedBoard: SparkFun RedBoard for Photon has the P1 module in an Arduino Uno R3 footprint. Please visit: www.sparkfun.com/products/13321
  OLED breakout: A DIP stand-in part for whatever IC you want. With 16 pins on a 300mil dual inline package (DIP) footprint.
  SWITCH-MOMENTARY-2: Various NO switches- pushbuttons, reed, etc
